# Fritzing sketch Cablage_maregraphe (saved by Fritzing 1.0.8)

parts:
  Connecteur_Subconn_Marégraphe = female pin header, 7 pins [form="♀ (female)"]
  Composant1 = SDM-SIO1 [package=dip]
  Data_Logger1 = Campbell Scientific CR-1000

nets:
  N1: Connecteur_Subconn_Marégraphe.pin1, Composant1.Z
  N2: Connecteur_Subconn_Marégraphe.pin2, Composant1.A
  N3: Connecteur_Subconn_Marégraphe.pin3, Data_Logger1.pin39
  N4: Connecteur_Subconn_Marégraphe.pin5, Composant1.Y
  N5: Connecteur_Subconn_Marégraphe.pin6, Composant1.B
  N6: Connecteur_Subconn_Marégraphe.pin7, Data_Logger1.pin38
  N7: Composant1.C1, Data_Logger1.pin42
  N8: Composant1.C2, Data_Logger1.pin43
  N9: Composant1.C3, Data_Logger1.pin44
  N10: Composant1.G, Data_Logger1.pin41

notes:
  Ground
  +12V
  Rouge/Noir

custom parts:
  SDM-SIO1: The SDM-SIO1 is a serial expansion module that allows a data logger to communicate with serial devices that interface using true RS-232, RS-422, or RS-485 signals. Up to fifteen SDM-SIO1 modules may be connected to a single data logger SDM interface. Remote serial devices use industry standard hardware and protocols to connect to the data logger through the SDM-SIO1 interface. When operating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
  Campbell Scientific CR-1000: This is a Fritzing part for the Campbell Scientific CR1000 datalogger. This is a common industrial data acquistion system.
